// Logisim project 0 CIRCUITO DO TRABALHO 0.circ as structural Verilog: 1 circuit, main circuit PC M++
module PC_M (
  input  Reset
);

  wire button_1_out, button_2_out, button_3_out, button_4_out, clock_1_out, undriven_3, undriven_4,
       undriven_5, undriven_8;
  wire [3:0] m_1_p1, m_1_p8, undriven, undriven_2;
  wire [7:0] rom_1_data, undriven_6;
  wire [15:0] undriven_7;

  // M m_1: pin names not known; wires that end beside it: m_1_p1[0], m_1_p1[1], m_1_p1[2], m_1_p1[3], m_1_p8[3], m_1_p8[2], m_1_p8[1], m_1_p8[0]
  Hex_Digit_Display hex_digit_display_1 (.value(m_1_p1));  // open: dp
  Hex_Digit_Display hex_digit_display_2 (.value(m_1_p8));  // open: dp
  Hex_Digit_Display hex_digit_display_3 (.value(undriven));  // open: dp
  Hex_Digit_Display hex_digit_display_4 (.value(undriven_2));  // open: dp
  Button button_1 (.out(button_1_out));
  Button button_2 (.out(button_2_out));
  Button button_3 (.out(button_3_out));
  Button button_4 (.out(button_4_out));
  Clock clock_1 (.out(clock_1_out));
  LED \Fim_de_Instrução  (.in(undriven_3));
  ROM #(.addrWidth(16)) rom_1 (.addr(undriven_7), .data(rom_1_data), .sel(undriven_8));
  RAM #(.bus("asynch")) ram_1 (.addr(undriven_6), .data(rom_1_data), .sel(undriven_4), .ld(undriven_5), .clr(Reset));

  // Notes on the sheet:
  //   +
  //   +
  //   -
  //   -
  //   ROM
  //   RAM
  //   contents of rom_1 (hex, n*v repeats v):
  //   7 c1 0 7 c9 0 7 d1 0 7 d9 0 c4 db cc d3 d4 cb dc c3 de 7 20 4 7 5 0 6b de 7 20 8 7 5 0 38 de 7 20 1
  //   7 5 0 d9 de 7 20 2 7 5 0 a6 7 3 0 c dc 7 20 0 7 5 0 5f 7 3 0 44 d4 7 20 0 7 5 0 54 d4 7 31 1 7 3 0 c
  //   7 d1 9 dc 7 39 1 7 3 0 c d4 7 20 0 7 5 0 c 7 3 0 44 dc 7 20 9 7 5 0 92 7 3 0 77 d4 7 11 1 d4 7 20 a
  //   7 5 0 87 7 3 0 c 7 d1 0 dc 7 19 1 7 3 0 c d4 7 20 9 7 5 0 c 7 3 0 9e d4 7 11 1 7 3 0 c cc 7 20 0 7 5
  //   0 cd 7 3 0 b2 c4 7 20 0 7 5 0 c2 c4 7 21 1 7 3 0 c 7 c1 9 cc 7 29 1 7 3 0 c c4 7 20 0 7 5 0 c 7 3 0
  //   b2 cc 7 20 9 7 5 1 0 7 3 0 e5 c4 7 1 1 c4 7 20 a 7 5 0 f5 7 3 0 c 7 c1 0 cc 7 9 1 7 3 0 c c4 7 20 9
  //   7 5 0 c 7 3 1 c c4 7 1 1 7 3 0 c 7 3 1 14
endmodule
