// Logisim project Addresser.circ as structural Verilog: 2 circuits, main circuit M Addresser 16bits
// MEM
module M_Addresser_16bits (
  input  _7,
  input  _6,
  input  _5,
  input  _4,
  input  _3,
  input  _2,
  input  _1,
  input  _0,
  input  S,
  input  CL,
  input  CH,
  input  R,
  input  PCH_BUS,
  input  PCL_BUS,
  output _31,
  output _30,
  output _29,
  output _28,
  output _27,
  output _26,
  output _25,
  output _24,
  output _15,
  output _14,
  output _13,
  output _12,
  output _11,
  output _10,
  output _9,
  output _8,
  output _23,
  output _22,
  output _21,
  output _20,
  output _19,
  output _18,
  output _17,
  output _16
);

  wire not_1_out, not_3_out, tri_state_8bits_1_p1, tri_state_8bits_1_p2, tri_state_8bits_1_p3,
       tri_state_8bits_1_p4, tri_state_8bits_1_p5, tri_state_8bits_1_p6, tri_state_8bits_1_p7,
       tri_state_8bits_1_p8, tri_state_8bits_1_p9, tri_state_8bits_2_p1, tri_state_8bits_3_p1,
       tri_state_8bits_3_p2, tri_state_8bits_3_p3, tri_state_8bits_3_p4, tri_state_8bits_3_p5,
       tri_state_8bits_3_p6, tri_state_8bits_3_p7, tri_state_8bits_3_p8, tri_state_8bits_4_p6,
       tri_state_8bits_4_p7, tri_state_8bits_4_p8, tri_state_8bits_4_p9, tri_state_8bits_4_p10,
       tri_state_8bits_4_p11, tri_state_8bits_4_p12, tri_state_8bits_4_p13, tri_state_8bits_5_p1,
       tri_state_8bits_5_p2, tri_state_8bits_5_p3, tri_state_8bits_5_p4, tri_state_8bits_5_p5,
       tri_state_8bits_5_p6, tri_state_8bits_5_p7, tri_state_8bits_5_p8, tri_state_8bits_6_p1;

  not not_1 (not_1_out, PCL_BUS);
  // Tri_State_8bits tri_state_8bits_1: pin names not known; wires that end beside it: tri_state_8bits_1_p1, tri_state_8bits_1_p2, tri_state_8bits_1_p3, tri_state_8bits_1_p4, tri_state_8bits_1_p5, tri_state_8bits_1_p6, tri_state_8bits_1_p7, tri_state_8bits_1_p8, tri_state_8bits_1_p9
  not not_2 (tri_state_8bits_1_p1, S);
  // Tri_State_8bits tri_state_8bits_2: pin names not known; wires that end beside it: tri_state_8bits_2_p1, _23, _31, _22, _30, _21, _29, _20, _28, _19, _27, _18, _26, _17, _25, _16, _24
  and and_1 (tri_state_8bits_2_p1, PCH_BUS, not_1_out);
  // Tri_State_8bits tri_state_8bits_3: pin names not known; wires that end beside it: tri_state_8bits_3_p1, tri_state_8bits_3_p2, tri_state_8bits_3_p3, tri_state_8bits_3_p4, tri_state_8bits_3_p5, tri_state_8bits_3_p6, tri_state_8bits_3_p7, tri_state_8bits_3_p8, S, _7, tri_state_8bits_1_p3, _6, tri_state_8bits_1_p5, _5, tri_state_8bits_1_p7, _4, tri_state_8bits_1_p9, _3, tri_state_8bits_3_p2, _2, tri_state_8bits_3_p4
  // Registrador_8_bits_S_Gatilho H: pin names not known; wires that end beside it: tri_state_8bits_1_p3, _23, tri_state_8bits_1_p5, _22, tri_state_8bits_1_p7, _21, tri_state_8bits_1_p9, _20, tri_state_8bits_3_p2, _19, tri_state_8bits_3_p4, _18, tri_state_8bits_3_p6, _17, tri_state_8bits_3_p8, _16, R, CH
  // Tri_State_8bits tri_state_8bits_4: pin names not known; wires that end beside it: _1, tri_state_8bits_3_p6, _0, tri_state_8bits_3_p8, tri_state_8bits_1_p1, tri_state_8bits_4_p6, tri_state_8bits_4_p7, tri_state_8bits_4_p8, tri_state_8bits_4_p9, tri_state_8bits_4_p10, tri_state_8bits_4_p11, tri_state_8bits_4_p12, tri_state_8bits_4_p13
  // Tri_State_8bits tri_state_8bits_5: pin names not known; wires that end beside it: tri_state_8bits_5_p1, tri_state_8bits_5_p2, tri_state_8bits_5_p3, tri_state_8bits_5_p4, tri_state_8bits_5_p5, tri_state_8bits_5_p6, tri_state_8bits_5_p7, tri_state_8bits_5_p8, S, _7, tri_state_8bits_4_p7, _6, tri_state_8bits_4_p9, _5, tri_state_8bits_4_p11, _4, tri_state_8bits_4_p13, _3, tri_state_8bits_5_p2, _2, tri_state_8bits_5_p4, _1, tri_state_8bits_5_p6, _0, tri_state_8bits_5_p8
  // Registrador_8_bits_S_Gatilho L: pin names not known; wires that end beside it: tri_state_8bits_4_p7, _15, tri_state_8bits_4_p9, _14, tri_state_8bits_4_p11, _13, tri_state_8bits_4_p13, _12, tri_state_8bits_5_p2, _11, tri_state_8bits_5_p4, _10, tri_state_8bits_5_p6, _9, tri_state_8bits_5_p8, _8, R, CL
  // Inc_16bits inc_16bits_1: pin names not known; wires that end beside it: _23, tri_state_8bits_1_p2, _22, tri_state_8bits_1_p4, _21, tri_state_8bits_1_p6, _20, tri_state_8bits_1_p8, _19, tri_state_8bits_3_p1, _18, tri_state_8bits_3_p3, _17, tri_state_8bits_3_p5, _16, tri_state_8bits_3_p7, _15, tri_state_8bits_4_p6, _14, tri_state_8bits_4_p8, _13, tri_state_8bits_4_p10, _12, tri_state_8bits_4_p12, _11, tri_state_8bits_5_p1
  // Tri_State_8bits tri_state_8bits_6: pin names not known; wires that end beside it: tri_state_8bits_6_p1, _15, _31, _14, _30, _13, _29, _12, _28, _11, _27, _10, _26, _9, _25, _8, _24
  and and_2 (tri_state_8bits_6_p1, PCL_BUS, not_3_out);
  not not_3 (not_3_out, PCH_BUS);

  // Notes on the sheet:
  //   Jean Jung
  //   Modulo de Endereçamento de Memória 16 Bits
  //   Seleção
  //   Clock L
  //   Clock H
  //   Reset
  //   16.. Output  ..8
  //   7.. Input  ..0
  //   7.. PC Bus  ..0
  //   7.. Output  ..0
endmodule

// Controller
module Control_Module (
  input  _7,
  input  _6,
  input  _5,
  input  _4,
  input  _3,
  input  _2,
  input  _1,
  input  _0,
  input  R,
  input  Clock,
  input  Flag_Z,
  input  Flag_C,
  output US0,
  output US1,
  output US2,
  output PBS0,
  output PBS1,
  output \Fim_de_Instrução ,
  output Sel_SP,
  output ULA_Bus,
  output BUF_Clock,
  output AC_Bus,
  output AC_Clock,
  output Reg_Bus,
  output Reg_Clock,
  output RAM_rd,
  output RAM_wr,
  output RAM_cs,
  output IN_bus,
  output OUT_clock,
  output ROM_rd,
  output ROM_cs,
  output PCH_bus,
  output PCL_bus,
  output PCH_Clock,
  output SelDataPC,
  output DIRClock,
  output SPIncDec,
  output PCL_Clock,
  output SP_Clock,
  output SP_Enable
);

  wire and_6_out, and_7_out, counter_5bits_1_p3, counter_5bits_1_p4, counter_5bits_1_p5, counter_5bits_1_p6,
       JC_p18, nor_2_out, or_2_out, RI_p20, tri_state_8bits_1_p1, tri_state_8bits_1_p2, tri_state_8bits_1_p4,
       tri_state_8bits_1_p5, tri_state_8bits_1_p7, tri_state_8bits_1_p8, tri_state_8bits_1_p10,
       tri_state_8bits_1_p11, tri_state_8bits_1_p13, tri_state_8bits_1_p14, tri_state_8bits_1_p16,
       tri_state_8bits_2_p1, tri_state_8bits_2_p3, tri_state_8bits_2_p4, tri_state_8bits_2_p6,
       tri_state_8bits_2_p8, tri_state_8bits_2_p10;
  wire [7:0] RI_p16, tri_state_8bits_2_p7, tri_state_8bits_2_p26;
  wire [11:0] rom_3_data;
  wire [15:12] RI_p19;

  nor nor_1 (\Fim_de_Instrução , tri_state_8bits_2_p7[0], tri_state_8bits_2_p7[1], tri_state_8bits_2_p7[2], tri_state_8bits_2_p7[3], tri_state_8bits_2_p7[4], tri_state_8bits_2_p7[5], tri_state_8bits_2_p7[6], tri_state_8bits_2_p7[7]);
  // Registrador_8_bits_S_Gatilho RI: pin names not known; wires that end beside it: _7, US2, _6, US1, _5, US0, _4, PBS1, _3, PBS0, _2, RI_p16[2], _1, RI_p16[1], _0, RI_p16[0], rom_3_data[3], 1'b0, RI_p19[12], RI_p20
  // Inc_8bits inc_8bits_1: pin names not known; wires that end beside it: tri_state_8bits_2_p7[7], tri_state_8bits_2_p7[6], tri_state_8bits_2_p7[5], tri_state_8bits_2_p7[4], tri_state_8bits_2_p7[3], tri_state_8bits_2_p7[2], tri_state_8bits_2_p7[1]
  // Tri_State_8bits tri_state_8bits_1: pin names not known; wires that end beside it: tri_state_8bits_1_p1, tri_state_8bits_1_p2, tri_state_8bits_1_p2, tri_state_8bits_1_p4, tri_state_8bits_1_p5, tri_state_8bits_1_p5, tri_state_8bits_1_p7, tri_state_8bits_1_p8, tri_state_8bits_1_p8, tri_state_8bits_1_p10, tri_state_8bits_1_p11, tri_state_8bits_1_p11, tri_state_8bits_1_p13, tri_state_8bits_1_p14, tri_state_8bits_1_p14, tri_state_8bits_1_p16
  not not_1 (tri_state_8bits_1_p1, rom_3_data[4]);
  and and_1 (RI_p16[3], RI_p19[12], RI_p20);
  // Counter_5bits counter_5bits_1: pin names not known; wires that end beside it: RI_p19[13], rom_3_data[5], counter_5bits_1_p3, counter_5bits_1_p4, counter_5bits_1_p5, counter_5bits_1_p6
  and and_2 (RI_p16[5], RI_p19[12], counter_5bits_1_p4);
  and and_3 (RI_p16[6], RI_p19[12], counter_5bits_1_p5);
  and and_4 (RI_p16[4], RI_p19[12], counter_5bits_1_p3);
  and and_5 (RI_p16[7], RI_p19[12], counter_5bits_1_p6);
  // Tri_State_8bits tri_state_8bits_2: pin names not known; wires that end beside it: tri_state_8bits_2_p1, tri_state_8bits_2_p1, tri_state_8bits_2_p3, tri_state_8bits_2_p4, tri_state_8bits_2_p4, tri_state_8bits_2_p6, tri_state_8bits_2_p7[0], tri_state_8bits_2_p8, tri_state_8bits_2_p8, tri_state_8bits_2_p10, rom_3_data[4], tri_state_8bits_2_p26[7], tri_state_8bits_1_p4, tri_state_8bits_1_p4, tri_state_8bits_2_p26[6], tri_state_8bits_1_p7, tri_state_8bits_2_p26[5], tri_state_8bits_1_p10, tri_state_8bits_2_p26[4], tri_state_8bits_1_p13, tri_state_8bits_2_p26[3], tri_state_8bits_1_p16, tri_state_8bits_2_p26[2], tri_state_8bits_2_p3, tri_state_8bits_2_p26[1], tri_state_8bits_2_p26[0]
  ROM rom_1 (.addr(RI_p16), .data(tri_state_8bits_2_p26));  // open: sel
  // Registrador_8_bits_S_Gatilho JC: pin names not known; wires that end beside it: tri_state_8bits_2_p7[7], tri_state_8bits_1_p7, tri_state_8bits_2_p7[6], tri_state_8bits_1_p10, tri_state_8bits_2_p7[5], tri_state_8bits_1_p13, tri_state_8bits_2_p7[4], tri_state_8bits_1_p16, tri_state_8bits_2_p7[3], tri_state_8bits_2_p3, tri_state_8bits_2_p7[2], tri_state_8bits_2_p6, tri_state_8bits_2_p6, tri_state_8bits_2_p7[1], tri_state_8bits_2_p10, tri_state_8bits_2_p10, tri_state_8bits_2_p7[0], JC_p18, Clock
  ROM #(.dataWidth(16)) rom_2 (
    .addr(tri_state_8bits_2_p7),
    .data({RI_p19, OUT_clock, IN_bus, RAM_cs, RAM_wr, RAM_rd, Reg_Clock, Reg_Bus, AC_Clock, AC_Bus, BUF_Clock, ULA_Bus, Sel_SP}));  // open: sel
  ROM #(.dataWidth(16)) rom_3 (
    .addr(tri_state_8bits_2_p7),
    .data({SPIncDec, SP_Clock, DIRClock, SelDataPC, rom_3_data[11:10], PCL_bus, PCH_bus, ROM_cs, ROM_rd, rom_3_data[5:0]}));  // open: sel
  or or_1 (JC_p18, R, rom_3_data[0]);
  nor nor_2 (nor_2_out, rom_3_data[2], rom_3_data[1]);
  and and_6 (and_6_out, rom_3_data[1], Flag_C);
  and and_7 (and_7_out, rom_3_data[2], Flag_Z);
  and and_8 (PCH_Clock, rom_3_data[10], or_2_out);
  or or_2 (or_2_out, nor_2_out, and_6_out, and_7_out);
  and and_9 (PCL_Clock, or_2_out, rom_3_data[11]);

  assign SP_Enable = SP_Clock;

  // Notes on the sheet:
  //   Jean Jung
  //   Módulo de Controle
  //   ULA
  //   PortBank
  //   7.. Input  ..0
  //   Decodificador de Instrução
  //   contents of rom_1 (hex, n*v repeats v):
  //   3 8 d 14 19 1e 25 2a 2c 31 36 3d 49 56 63 2a 7f 84 8b 91 94 98 9b 2a 7*0 2a 7*0 2a 7*0 2a 7*0 2a 7*0
  //   2a 7*0 2a 7*0 2a 7*0 2a 7*0 2a 7*0 2a 7*0 2a 7*0 2a 7*0 2a 7*0 2a 7*0 2a 7*0 2a 7*0 2a 7*0 2a 7*0 2a
  //   7*0 2a 7*0 2a 7*0 2a 7*0 2a 7*0 2a 7*0 2a 7*0 2a 7*0 2a 7*0 2a 7*0 2a
  //   Controle B
  //   Controle A
  //   contents of rom_2 (hex, n*v repeats v):
  //   2000 0 0 8 4 2 10 0 8 4 2 40 0 0 0 8 4 2 302 0 8 c 2 800 0 20 4 2 10 0 0 0 280 4 2 10 0 400 4 2 10 0
  //   0 1000 0 4 2 10 0 0 4 2 40 0 0 4 0 0 2 302 0 0 1 301 0 0 1 301 281 0 281 0 0 0 1 301 0 0 1 301 0 281
  //   0 281 0 0 0 1 301 0 0 1 301 0 281 0 281 6*0 1 301 0 0 1 301 5*0 1 301 1 301 4*0 281 0 281 0 0 281 0
  //   281 0 0 20 20 280 4 2 10 0 20 20 8 4 2 302 0 20 321 281 2c1 0 0 0 8 309 281 291
  //   HD
  //   HD Res
  //   CRes
  //   CResC
  //   CResZ
  //   RIClock
  //   SeIRI
  //   HD Clock
  //   contents of rom_3 (hex, n*v repeats v):
  //   0 c0 c18 4*0 1 4*0 1 c0 2c00 4*0 1 4*0 1 4*0 1 c0 2c00 4*0 1 4*0 1 e0 c18 c0 c00 0 0 1 c0 c00 0 0 1
  //   c0 c00 c0 2c00 0 0 1 8000 c0c0 80c0 c00 80c0 c0c0 c0 1000 4800 1000 4400 1 8000 c0c0 80c0 c00 80c0
  //   c0c0 c0 c00 1002 4802 1002 4402 1 8000 c0c0 80c0 c00 80c0 c0c0 c0 c00 1004 4804 1004 4404 1 8000
  //   c000 8000 c000 80c0 c0c0 c00 80c0 c0c0 c0 c00 4000 0 4000 0 4000 8100 c200 200 8000 c000 8000 c000
  //   1000 4800 1000 4400 1 1000 4800 1000 4400 1 0 2000 4*0 1 0 2000 0 0 0 1 8000 c000 1 0 0 4000 1 8000
  //   c000 1 0 0 4000 1
  //   Clock PCH
  //   Clock PCL
  //   SP Clock
endmodule
