// Logisim project PC.circ as structural Verilog: 1 circuit, main circuit PC M++
module PC_M (
  input  _7,
  input  _6,
  input  _5,
  input  _4,
  input  _3,
  input  _2,
  input  _1,
  input  _0,
  input  _7_2,
  input  _6_2,
  input  _5_2,
  input  _4_2,
  input  _3_2,
  input  _2_2,
  input  _1_2,
  input  _0_2,
  input  _7_3,
  input  _6_3,
  input  _5_3,
  input  _4_3,
  input  _3_3,
  input  _2_3,
  input  _1_3,
  input  _0_3,
  input  _0_4,
  input  _1_4,
  input  _2_4,
  input  _3_4,
  input  _4_4,
  input  _5_4,
  input  _6_4,
  input  _7_4,
  input  Reset
);

  wire clock_1_out, m_1_p9, m_1_p10, m_1_p11, m_1_p12, m_1_p13, m_1_p14, m_1_p15, m_1_p16, m_1_p34, m_1_p36,
       m_1_p38, undriven, undriven_2, undriven_3, undriven_4, undriven_5, undriven_6, undriven_7, undriven_8,
       undriven_9, undriven_10, undriven_11, undriven_12, undriven_13, undriven_14, undriven_15, undriven_16,
       undriven_17;
  wire [3:0] m_1_p24, m_1_p32;
  wire [7:0] rom_1_data, undriven_18;
  wire [15:0] undriven_19;

  Hex_Digit_Display hex_digit_display_1 (.value(m_1_p24));  // open: dp
  // M m_1: pin names not known; wires that end beside it: _0_4, _1_4, _2_4, _3_4, _4_4, _5_4, _6_4, _7_4, m_1_p9, m_1_p10, m_1_p11, m_1_p12, m_1_p13, m_1_p14, m_1_p15, m_1_p16, _7, m_1_p24[3], _6, m_1_p24[2], _5, m_1_p24[1], _4, m_1_p24[0], _3, m_1_p32[3], _2, m_1_p32[2], _1, m_1_p32[1], _0, m_1_p32[0], _7_2, m_1_p34, _6_2, m_1_p36, _5_2, m_1_p38
  LED u__0 (.in(m_1_p9));
  LED u__1 (.in(m_1_p10));
  LED u__2 (.in(m_1_p11));
  LED u__3 (.in(m_1_p12));
  LED u__4 (.in(m_1_p13));
  LED u__5 (.in(m_1_p14));
  LED u__6 (.in(m_1_p15));
  LED u__7 (.in(m_1_p16));
  Hex_Digit_Display hex_digit_display_2 (.value(m_1_p32));  // open: dp
  LED u__7_2 (.in(m_1_p34));
  LED u__5_2 (.in(m_1_p38));
  LED u__4_2 (.in(undriven));
  LED u__3_2 (.in(undriven_2));
  LED u__6_2 (.in(m_1_p36));
  LED u__2_2 (.in(undriven_3));
  LED u__0_2 (.in(undriven_5));
  LED u__7_3 (.in(undriven_6));
  LED u__1_2 (.in(undriven_4));
  LED u__5_3 (.in(undriven_8));
  LED u__4_3 (.in(undriven_9));
  LED u__3_3 (.in(undriven_10));
  LED u__6_3 (.in(undriven_7));
  Clock clock_1 (.out(clock_1_out));
  LED u__0_3 (.in(undriven_13));
  LED u__1_3 (.in(undriven_12));
  LED u__2_3 (.in(undriven_11));
  LED \Fim_de_Instrução  (.in(undriven_14));
  ROM #(.addrWidth(16)) rom_1 (.addr(undriven_19), .data(rom_1_data), .sel(undriven_16));
  RAM #(.bus("asynch")) ram_1 (.addr(undriven_18), .data(rom_1_data), .sel(undriven_15), .ld(undriven_17), .clr(Reset));

  // Notes on the sheet:
  //   ROM
  //   RAM
  //   contents of rom_1 (hex, n*v repeats v):
  //   7 c0 1 e0 c1 e0 c9 e0 d1 e0 d9 7 7 3 7 7 b 7 7 13 7 7 1b 7 6 0 33 7 7 1c 7 7 14 7 7 c 7 7 4 c4 c3 cc
  //   cb d4 d3 dc db 7 3 0 2f 7 c0 0 c1 c9 d1 d9 7 7
endmodule
