// Logisim project PCerror.circ as structural Verilog: 1 circuit, main circuit PC M++
module PC_M (
  input  _7,
  input  _6,
  input  _5,
  input  _4,
  input  _3,
  input  _2,
  input  _1,
  input  _0,
  input  _7_2,
  input  _6_2,
  input  _5_2,
  input  _4_2,
  input  _3_2,
  input  _2_2,
  input  _1_2,
  input  _0_2,
  input  _0_3,
  input  _1_3,
  input  _2_3,
  input  _3_3,
  input  _4_3,
  input  _5_3,
  input  _6_3,
  input  _7_3,
  input  Reset
);

  wire clock_1_out, keyboard_1_avail, m_1_p1, m_1_p2, m_1_p3, m_1_p4, m_1_p5, m_1_p6, m_1_p7, m_1_p16,
       m_1_p41, m_1_p43, m_1_p45, undriven, undriven_2, undriven_3, undriven_4, undriven_6, undriven_7,
       undriven_8, undriven_9, undriven_10;
  wire [3:0] m_1_p31, m_1_p39;
  wire [6:0] keyboard_1_data, undriven_5;
  wire [7:0] rom_1_data, undriven_11;
  wire [15:0] undriven_12;

  Hex_Digit_Display hex_digit_display_1 (.value(m_1_p31));  // open: dp
  // M m_1: pin names not known; wires that end beside it: m_1_p1, m_1_p2, m_1_p3, m_1_p4, m_1_p5, m_1_p6, m_1_p7, _0_3, _1_3, _2_3, _3_3, _4_3, _5_3, _6_3, _7_3, m_1_p16, m_1_p1, m_1_p2, m_1_p3, m_1_p4, m_1_p5, m_1_p6, m_1_p7, _7, m_1_p31[3], _6, m_1_p31[2], _5, m_1_p31[1], _4, m_1_p31[0], _3, m_1_p39[3], _2, m_1_p39[2], _1, m_1_p39[1], _0, m_1_p39[0], _7_2, m_1_p41, _6_2, m_1_p43, _5_2, m_1_p45
  Hex_Digit_Display hex_digit_display_2 (.value(m_1_p39));  // open: dp
  Keyboard keyboard_1 (.clk(m_1_p16), .avail(keyboard_1_avail), .data(keyboard_1_data));  // open: re, clr
  LED u__7 (.in(m_1_p41));
  LED u__3 (.in(undriven_2));
  LED u__4 (.in(undriven));
  LED u__6 (.in(m_1_p43));
  LED u__5 (.in(m_1_p45));
  LED u__2 (.in(undriven_3));
  LED u__0 (.in(undriven_6));
  LED u__1 (.in(undriven_4));
  Clock clock_1 (.out(clock_1_out));
  LED \Fim_de_Instrução  (.in(undriven_7));
  TTY tty_1 (.data(undriven_5));  // open: clk, we, clr
  ROM #(.addrWidth(16)) rom_1 (.addr(undriven_12), .data(rom_1_data), .sel(undriven_9));
  RAM #(.bus("asynch")) ram_1 (.addr(undriven_11), .data(rom_1_data), .sel(undriven_8), .ld(undriven_10), .clr(Reset));

  // Notes on the sheet:
  //   ROM
  //   contents of rom_1 (hex, n*v repeats v):
  //   7 6 0 10 7 6 0 22 7 6 0 33 7 3 0 0 de 7 40 80 7 20 80 7 5 0 1f 7 3 0 10 7 7 0 de 7 40 7f c1 7 c0 1
  //   c3 7 c0 0 c3 c4 7 7 0 db 7 7
endmodule
